// Logisim project Befunge.circ as structural Verilog: 4 circuits, main circuit Befunge
module Befunge (
  input  Reset
);

  wire [7:0] program_1_instr_out;
  wire [31:0] control_1_ctrl_out, control_1_stack_out, stack_1_stack_out;

  Clock clock_1 ();  // open: out
  Program program_1 (.Instr_OUT(program_1_instr_out), .Ctrl_IN(control_1_ctrl_out), .RESET(Reset));
  Control control_1 (
    .Instr_IN(program_1_instr_out), .Ctrl_OUT(control_1_ctrl_out), .Stack_OUT(control_1_stack_out),
    .Stack_IN(stack_1_stack_out));
  Stack stack_1 (.Stack_IN(control_1_stack_out), .Stack_OUT(stack_1_stack_out), .Ctrl_IN(control_1_ctrl_out));
endmodule

// STACK
module Stack (
  input  [31:0] Stack_IN,
  input  [31:0] Ctrl_IN,
  output [31:0] Stack_OUT
);

  wire clock_1_out, not_1_out, or_1_out;
  wire [23:0] adder_1_out, controlled_buffer_1_out, controlled_buffer_3_out, register_1_q, subtractor_1_out;

  assign controlled_buffer_1_out = Ctrl_IN[16] ? adder_1_out : 24'bz;  // Controlled_Buffer controlled_buffer_1
  assign controlled_buffer_1_out = Ctrl_IN[15] ? subtractor_1_out : 24'bz;  // Controlled_Buffer controlled_buffer_2
  or or_1 (or_1_out, Ctrl_IN[15], Ctrl_IN[16]);
  Adder #(.width(24)) adder_1 (.a(register_1_q), .b(24'h1), .out(adder_1_out));  // open: cin, cout
  Subtractor #(.width(24)) subtractor_1 (.a(register_1_q), .b(24'h1), .out(subtractor_1_out));  // open: bin, bout
  Register #(.width(24)) register_1 (
    .D(controlled_buffer_1_out), .en(or_1_out), .Q(register_1_q), .clk(clock_1_out));  // open: clr
  assign controlled_buffer_3_out = not_1_out ? register_1_q : 24'bz;  // Controlled_Buffer controlled_buffer_3
  not not_1 (not_1_out, Ctrl_IN[15]);
  assign controlled_buffer_3_out = Ctrl_IN[15] ? subtractor_1_out : 24'bz;  // Controlled_Buffer controlled_buffer_4
  Clock clock_1 (.out(clock_1_out));
  RAM #(.addrWidth(24), .dataWidth(32), .bus("separate")) ram_1 (
    .addr(controlled_buffer_3_out), .din(Stack_IN), .data(Stack_OUT), .str(Ctrl_IN[16]), .clk(clock_1_out),
    .ld(Ctrl_IN[15]));  // open: sel, clr

  // Notes on the sheet:
  //   PUSH
  //   POP
endmodule

// PROG
module Program (
  input  RESET,
  input  [31:0] Ctrl_IN,
  output [7:0] Instr_OUT
);

  wire clock_1_out, controlled_buffer_2_out, nor_1_out, nor_2_out, not_1_out, or_1_out, or_2_out, or_3_out;
  wire [3:0] controlled_buffer_1_out, controlled_buffer_7_out, Dir_q;
  wire [11:0] adder_1_out, adder_2_out, bit_extender_1_out, controlled_buffer_5_out, controlled_buffer_6_out,
       controlled_buffer_10_out, subtractor_1_out, subtractor_2_out, X_q, Y_q;

  assign controlled_buffer_1_out = RESET ? 4'b0001 : 4'bz;  // Controlled_Buffer controlled_buffer_1
  assign controlled_buffer_2_out = RESET ? 1'b1 : 1'bz;  // Controlled_Buffer controlled_buffer_2
  assign controlled_buffer_2_out = not_1_out ? Ctrl_IN[5] : 1'bz;  // Controlled_Buffer controlled_buffer_3
  not not_1 (not_1_out, RESET);
  assign controlled_buffer_1_out = not_1_out ? Ctrl_IN[4:1] : 4'bz;  // Controlled_Buffer controlled_buffer_4
  assign bit_extender_1_out = {{4{1'b0}}, Ctrl_IN[13:6]};  // Bit_Extender bit_extender_1
  or or_1 (or_1_out, RESET, clock_1_out);
  nor nor_1 (nor_1_out, controlled_buffer_7_out[0], controlled_buffer_7_out[1]);
  assign controlled_buffer_5_out = nor_1_out ? bit_extender_1_out : 12'bz;  // Controlled_Buffer controlled_buffer_5
  nor nor_2 (nor_2_out, controlled_buffer_7_out[2], controlled_buffer_7_out[3]);
  assign controlled_buffer_6_out = nor_2_out ? bit_extender_1_out : 12'bz;  // Controlled_Buffer controlled_buffer_6
  assign controlled_buffer_7_out = Ctrl_IN[0] ? Dir_q : 4'bz;  // Controlled_Buffer controlled_buffer_7
  Pull_Resistor pull_resistor_1 (.node(controlled_buffer_7_out));
  Register #(.width(4), .trigger("high")) Dir (
    .D(controlled_buffer_1_out), .en(controlled_buffer_2_out), .Q(Dir_q), .clk(or_1_out));  // open: clr
  assign controlled_buffer_5_out = or_2_out ? controlled_buffer_10_out : 12'bz;  // Controlled_Buffer controlled_buffer_8
  or or_2 (or_2_out, controlled_buffer_7_out[0], controlled_buffer_7_out[1]);
  assign controlled_buffer_6_out = or_3_out ? controlled_buffer_10_out : 12'bz;  // Controlled_Buffer controlled_buffer_9
  or or_3 (or_3_out, controlled_buffer_7_out[2], controlled_buffer_7_out[3]);
  Clock clock_1 (.out(clock_1_out));
  Register #(.width(12), .trigger("falling")) X (
    .D(controlled_buffer_5_out), .en(or_2_out), .Q(X_q), .clk(clock_1_out));  // open: clr
  Register #(.width(12), .trigger("falling")) Y (
    .D(controlled_buffer_6_out), .en(or_3_out), .Q(Y_q), .clk(clock_1_out));  // open: clr
  assign controlled_buffer_10_out = controlled_buffer_7_out[0] ? adder_1_out : 12'bz;  // Controlled_Buffer controlled_buffer_10
  Adder #(.width(12)) adder_1 (.a(X_q), .b(12'h1), .out(adder_1_out));  // open: cin, cout
  Adder #(.width(12)) adder_2 (.a(Y_q), .b(12'h1), .out(adder_2_out));  // open: cin, cout
  assign controlled_buffer_10_out = controlled_buffer_7_out[2] ? adder_2_out : 12'bz;  // Controlled_Buffer controlled_buffer_11
  assign controlled_buffer_10_out = controlled_buffer_7_out[1] ? subtractor_1_out : 12'bz;  // Controlled_Buffer controlled_buffer_12
  Subtractor #(.width(12)) subtractor_1 (.a(X_q), .b(12'h1), .out(subtractor_1_out));  // open: bin, bout
  assign controlled_buffer_10_out = controlled_buffer_7_out[3] ? subtractor_2_out : 12'bz;  // Controlled_Buffer controlled_buffer_13
  Subtractor #(.width(12)) subtractor_2 (.a(Y_q), .b(12'h1), .out(subtractor_2_out));  // open: bin, bout
  RAM #(.addrWidth(24), .bus("separate")) ram_1 (
    .addr({Y_q, X_q}), .din(Ctrl_IN[13:6]), .data(Instr_OUT), .str(Ctrl_IN[14]), .clk(clock_1_out));  // open: sel, ld, clr

  // Notes on the sheet:
  //   Dir-IN
  //   Dir-EN
  //   Next-Instr
  //   Put
endmodule

// CONTROL
module Control (
  input  [7:0] Instr_IN,
  input  [31:0] Stack_IN,
  output [31:0] Stack_OUT,
  output [31:0] Ctrl_OUT
);

  wire clock_1_out, clock_2_out, comparator_1_eq, comparator_2_eq, comparator_3_eq, comparator_4_eq,
       comparator_5_eq, comparator_6_eq, comparator_7_eq, comparator_8_eq, comparator_9_eq, comparator_10_eq,
       comparator_11_eq, comparator_12_eq, comparator_13_eq, comparator_14_eq, comparator_15_eq,
       comparator_16_eq, comparator_17_eq, comparator_18_eq, comparator_19_gt, decoder_1_out1,
       decoder_1_out2, decoder_1_out3, decoder_1_out4, decoder_1_out5, decoder_1_out6, decoder_1_out7,
       not_1_out, not_2_out;
  wire [7:0] adder_1_out, controlled_buffer_1_out, counter_1_q;
  wire [31:0] adder_2_out, bit_extender_1_out, bit_extender_2_out, bit_extender_3_out, divider_1_out,
       divider_2_rem, multiplier_1_out, R0_q, R1_q, subtractor_1_out;

  Comparator comparator_1 (.a(Instr_IN), .b(8'h30), .eq(comparator_1_eq));  // open: gt, lt
  Comparator comparator_2 (.a(Instr_IN), .b(8'h31), .eq(comparator_2_eq));  // open: gt, lt
  Comparator comparator_3 (.a(Instr_IN), .b(8'h32), .eq(comparator_3_eq));  // open: gt, lt
  Comparator comparator_4 (.a(Instr_IN), .b(8'h33), .eq(comparator_4_eq));  // open: gt, lt
  Comparator comparator_5 (.a(Instr_IN), .b(8'h34), .eq(comparator_5_eq));  // open: gt, lt
  Comparator comparator_6 (.a(Instr_IN), .b(8'h35), .eq(comparator_6_eq));  // open: gt, lt
  Comparator comparator_7 (.a(Instr_IN), .b(8'h36), .eq(comparator_7_eq));  // open: gt, lt
  Comparator comparator_8 (.a(Instr_IN), .b(8'h37), .eq(comparator_8_eq));  // open: gt, lt
  Comparator comparator_9 (.a(Instr_IN), .b(8'h38), .eq(comparator_9_eq));  // open: gt, lt
  Comparator comparator_10 (.a(Instr_IN), .b(8'h39), .eq(comparator_10_eq));  // open: gt, lt
  Comparator comparator_11 (.a(Instr_IN), .b(8'h2b), .eq(comparator_11_eq));  // open: gt, lt
  Comparator comparator_12 (.a(Instr_IN), .b(8'h2d), .eq(comparator_12_eq));  // open: gt, lt
  Comparator comparator_13 (.a(Instr_IN), .b(8'h2a), .eq(comparator_13_eq));  // open: gt, lt
  Comparator comparator_14 (.a(Instr_IN), .b(8'h2f), .eq(comparator_14_eq));  // open: gt, lt
  Comparator comparator_15 (.a(Instr_IN), .b(8'h25), .eq(comparator_15_eq));  // open: gt, lt
  Comparator comparator_16 (.a(Instr_IN), .b(8'h21), .eq(comparator_16_eq));  // open: gt, lt
  Comparator comparator_17 (.a(Instr_IN), .b(8'h60), .eq(comparator_17_eq));  // open: gt, lt
  assign controlled_buffer_1_out = comparator_1_eq ? 8'h1 : 8'bz;  // Controlled_Buffer controlled_buffer_1
  assign controlled_buffer_1_out = comparator_2_eq ? 8'h2 : 8'bz;  // Controlled_Buffer controlled_buffer_2
  assign controlled_buffer_1_out = comparator_3_eq ? 8'h3 : 8'bz;  // Controlled_Buffer controlled_buffer_3
  assign controlled_buffer_1_out = comparator_4_eq ? 8'h4 : 8'bz;  // Controlled_Buffer controlled_buffer_4
  assign controlled_buffer_1_out = comparator_5_eq ? 8'h5 : 8'bz;  // Controlled_Buffer controlled_buffer_5
  assign controlled_buffer_1_out = comparator_6_eq ? 8'h6 : 8'bz;  // Controlled_Buffer controlled_buffer_6
  assign controlled_buffer_1_out = comparator_7_eq ? 8'h7 : 8'bz;  // Controlled_Buffer controlled_buffer_7
  assign controlled_buffer_1_out = comparator_8_eq ? 8'h8 : 8'bz;  // Controlled_Buffer controlled_buffer_8
  assign controlled_buffer_1_out = comparator_9_eq ? 8'h9 : 8'bz;  // Controlled_Buffer controlled_buffer_9
  assign controlled_buffer_1_out = comparator_10_eq ? 8'ha : 8'bz;  // Controlled_Buffer controlled_buffer_10
  assign controlled_buffer_1_out = comparator_11_eq ? 8'hb : 8'bz;  // Controlled_Buffer controlled_buffer_11
  assign controlled_buffer_1_out = comparator_12_eq ? 8'hf : 8'bz;  // Controlled_Buffer controlled_buffer_12
  assign controlled_buffer_1_out = comparator_13_eq ? 8'h13 : 8'bz;  // Controlled_Buffer controlled_buffer_13
  assign controlled_buffer_1_out = comparator_14_eq ? 8'h17 : 8'bz;  // Controlled_Buffer controlled_buffer_14
  assign controlled_buffer_1_out = comparator_15_eq ? 8'h1b : 8'bz;  // Controlled_Buffer controlled_buffer_15
  assign controlled_buffer_1_out = comparator_16_eq ? 8'h1f : 8'bz;  // Controlled_Buffer controlled_buffer_16
  assign controlled_buffer_1_out = comparator_17_eq ? 8'h22 : 8'bz;  // Controlled_Buffer controlled_buffer_17
  Pull_Resistor pull_resistor_1 (.node(controlled_buffer_1_out));
  not not_1 (not_1_out, Ctrl_OUT[0]);
  Counter counter_1 (
    .load(1'b0), .count(not_1_out), .Q(counter_1_q), .clk(clock_1_out), .clr(not_2_out));  // open: D, carry
  Clock clock_1 (.out(clock_1_out));
  Adder adder_1 (.a(counter_1_q), .b(controlled_buffer_1_out), .out(adder_1_out));  // open: cin, cout
  not not_2 (not_2_out, Ctrl_OUT[17]);
  Decoder #(.select(4)) decoder_1 (
    .out1(decoder_1_out1), .out2(decoder_1_out2), .out3(decoder_1_out3), .out4(decoder_1_out4),
    .out5(decoder_1_out5), .out6(decoder_1_out6), .out7(decoder_1_out7), .sel(Ctrl_OUT[28:25]));  // open: out0, out8, out9, out10, out11, out12, out13, out14, out15, en
  Pull_Resistor pull_resistor_2 (.node(Stack_OUT));
  Pull_Resistor pull_resistor_3 (.node(Ctrl_OUT));
  ROM #(.dataWidth(32)) rom_1 (.addr(adder_1_out), .data(Ctrl_OUT));  // open: sel
  assign bit_extender_1_out = {{28{1'b0}}, Ctrl_OUT[21:18]};  // Bit_Extender bit_extender_1
  assign Stack_OUT = Ctrl_OUT[22] ? bit_extender_1_out : 32'bz;  // Controlled_Buffer controlled_buffer_18
  assign Stack_OUT = decoder_1_out1 ? adder_2_out : 32'bz;  // Controlled_Buffer controlled_buffer_19
  assign Stack_OUT = decoder_1_out2 ? subtractor_1_out : 32'bz;  // Controlled_Buffer controlled_buffer_20
  assign Stack_OUT = decoder_1_out3 ? multiplier_1_out : 32'bz;  // Controlled_Buffer controlled_buffer_21
  assign Stack_OUT = decoder_1_out4 ? divider_1_out : 32'bz;  // Controlled_Buffer controlled_buffer_22
  assign Stack_OUT = decoder_1_out5 ? divider_2_rem : 32'bz;  // Controlled_Buffer controlled_buffer_23
  assign Stack_OUT = decoder_1_out6 ? bit_extender_2_out : 32'bz;  // Controlled_Buffer controlled_buffer_24
  assign Stack_OUT = decoder_1_out7 ? bit_extender_3_out : 32'bz;  // Controlled_Buffer controlled_buffer_25
  Register #(.width(32)) R0 (.D(Stack_IN), .en(Ctrl_OUT[23]), .Q(R0_q), .clk(clock_2_out));  // open: clr
  Register #(.width(32)) R1 (.D(Stack_IN), .en(Ctrl_OUT[24]), .Q(R1_q), .clk(clock_2_out));  // open: clr
  Clock clock_2 (.out(clock_2_out));
  Adder #(.width(32)) adder_2 (.a(R1_q), .b(R0_q), .out(adder_2_out));  // open: cin, cout
  Subtractor #(.width(32)) subtractor_1 (.a(R1_q), .b(R0_q), .out(subtractor_1_out));  // open: bin, bout
  Multiplier #(.width(32)) multiplier_1 (.a(R1_q), .b(R0_q), .out(multiplier_1_out));  // open: cin, cout
  Divider #(.width(32)) divider_1 (.a(R1_q), .b(R0_q), .out(divider_1_out));  // open: upper, rem
  Divider #(.width(32)) divider_2 (.a(R1_q), .b(R0_q), .rem(divider_2_rem));  // open: out, upper
  Comparator #(.width(32), .mode("unsigned")) comparator_18 (
    .a(R0_q), .b({32{1'b0}}), .eq(comparator_18_eq));  // open: gt, lt
  Comparator #(.width(32), .mode("unsigned")) comparator_19 (
    .a(R1_q), .b(R0_q), .gt(comparator_19_gt));  // open: eq, lt
  assign bit_extender_2_out = {{31{1'b0}}, comparator_18_eq};  // Bit_Extender bit_extender_2
  assign bit_extender_3_out = {{31{1'b0}}, comparator_19_gt};  // Bit_Extender bit_extender_3

  // Notes on the sheet:
  //   0
  //   1
  //   2
  //   3
  //   4
  //   5
  //   6
  //   7
  //   8
  //   9
  //   +
  //   -
  //   *
  //   /
  //   %
  //   !
  //   `
  //   contents of rom_1 (hex, n*v repeats v):
  //   1 410001 450001 490001 4d0001 510001 550001 590001 5d0001 610001 650001 828000 1028000 2030000 20001
  //   828000 1028000 4030000 20001 828000 1028000 6030000 20001 828000 1028000 8030000 20001 828000
  //   1028000 a030000 20001 828000 c030000 20001 828000 1028000 e030000 20001
endmodule
